# Fritzing sketch BioReactor (saved by Fritzing 1.0.4)
breadboards: 1

parts:
  Part1 = Arduino Mega 2560 (Rev3)
  Q1 = Basic FET P-Channel [package="D2Pak [SMD]"]
  R1 = Resistor [tolerance=±5% power=0.25W resistance=220 package=THT]

nets:
  N1: Part1.D9_PWM, R1.Pin_0
  N2: Q1.Gate, R1.Pin_1
